# Fritzing sketch schema (saved by Fritzing 0.9.2b)
breadboards: 1

parts:
  OLED1 = 128x64 Monochrom OLED Display with SPI Control
  Part1 = Arduino Yun

nets:
  N1: OLED1.Data, Part1.D9_PWM
  N2: OLED1.Clock, Part1.D10_PWM/SS
  N3: OLED1.SA0/DC, Part1.D11_PWM/MOSI
  N4: OLED1.Reset, Part1.D13/SCK
  N5: OLED1.CS, Part1.D12/MISO
  3V3: OLED1.3v3, OLED1.Vin, Part1.5V
